# Fritzing sketch openBeatsV1 (saved by Fritzing 0.9.5d)
breadboards: 3

parts:
  J1 = STM32 Nucleo boards
  S2 = Pushbutton [package="[THT]"]
  S3 = Pushbutton [package="[THT]"]
  S4 = Pushbutton [package="[THT]"]
  S5 = Pushbutton [package="[THT]"]
  S6 = Pushbutton [package="[THT]"]
  S7 = Pushbutton [package="[THT]"]
  S8 = Pushbutton [package="[THT]"]
  S9 = Pushbutton [package="[THT]"]
  IC1 = IC, DIP package, 28 pins [chip_label=TLC5940]
  LED2 = LED - 5mm [color="Red (633nm)" package="5 mm [THT]"]
  LED3 = LED - 5mm [color="Red (633nm)" package="5 mm [THT]"]
  LED4 = LED - 5mm [color="Red (633nm)" package="5 mm [THT]"]
  LED5 = LED - 5mm [color="Red (633nm)" package="5 mm [THT]"]
  LED6 = LED - 5mm [color="Red (633nm)" package="5 mm [THT]"]
  LED7 = LED - 5mm [color="Red (633nm)" package="5 mm [THT]"]
  LED8 = LED - 5mm [color="Red (633nm)" package="5 mm [THT]"]
  LED9 = LED - 5mm [color="Red (633nm)" package="5 mm [THT]"]
  Part1 = Analog Digital MUX Breakout
  R1 = Resistor [tolerance=±5% resistance=1.5k package=THT]
  R2 = Resistor [tolerance=±5% resistance=1.5k package=THT]
  R3 = Resistor [tolerance=±5% resistance=1.5k package=THT]
  R4 = Resistor [tolerance=±5% resistance=1.5k package=THT]
  R5 = Resistor [tolerance=±5% resistance=1.5k package=THT]
  R6 = Resistor [tolerance=±5% resistance=1.5k package=THT]
  R7 = Resistor [tolerance=±5% resistance=1.5k package=THT]
  R8 = Resistor [tolerance=±5% resistance=1.5k package=THT]
  C1 = Electrolytic Capacitor [capacitance=4.7µF voltage=50V package="100 mil [THT, electrolytic]"]
  C2 = Ceramic Capacitor [capacitance=0.22µF voltage=50V package="100 mil [THT, multilayer]"]
  R9 = Resistor [tolerance=±5% resistance=2.2k package=THT]
  RE1 = Hexadecimal Rotary Encoder [part_number="Stand i9n" package=THT]
  JP1 = Header 6 [package=1x06-smd-female]
  SP1 = SPEAKER [package=pcb_mount_speaker]
  IC3 = IC, DIP package, 14 pins [chip_label=CD40106BE]
  R10 = Resistor [tolerance=±5% resistance=10k package=THT]
  R11 = Resistor [tolerance=±5% resistance=47k package=THT]
  SP2 = SPEAKER [package=pcb_mount_speaker]
  SP3 = SPEAKER [package=pcb_mount_speaker]
  SP4 = SPEAKER [package=pcb_mount_speaker]
  C3 = Ceramic Capacitor [capacitance=0.22µF voltage=50V package="100 mil [THT, multilayer]"]
  R12 = Resistor [tolerance=±5% resistance=10k package=THT]
  R13 = Resistor [tolerance=±5% resistance=47k package=THT]
  R14 = Resistor [tolerance=±5% resistance=10k package=THT]
  R15 = Resistor [tolerance=±5% resistance=47k package=THT]
  R16 = Resistor [tolerance=±5% resistance=10k package=THT]
  R17 = Resistor [tolerance=±5% resistance=47k package=THT]
  C4 = Ceramic Capacitor [capacitance=0.22µF voltage=50V package="100 mil [THT, multilayer]"]
  C5 = Ceramic Capacitor [capacitance=0.22µF voltage=50V package="100 mil [THT, multilayer]"]
  C6 = Ceramic Capacitor [capacitance=0.22µF voltage=50V package="100 mil [THT, multilayer]"]
  R18 = Resistor [tolerance=±5% resistance=100k package=THT]
  R19 = Resistor [tolerance=±5% resistance=100k package=THT]
  R20 = Resistor [tolerance=±5% resistance=100k package=THT]
  R21 = Resistor [tolerance=±5% resistance=100k package=THT]
  C7 = Ceramic Capacitor [capacitance=100nF voltage=50V package="100 mil [THT, multilayer]"]
  JP2 = Header 6 [package=1x06-smd-female]

nets:
  N1: J1.A2, RE1.Output4Pin
  N2: J1.A3, RE1.Output1Pin
  N3: J1.A4/SDA, RE1.Output8pin
  N4: J1.A5/SCL, RE1.Output2Pin
  N5: J1.GND#880, C1.-, C2.0
  N6: J1.D9_PWM, Part1.S2
  N7: J1.D2, Part1.EN
  N8: J1.D3_PWM, Part1.SIG
  N9: J1.D5_PWM, Part1.S0
  N10: J1.D6_PWM, Part1.S1
  N11: J1.D7, Part1.S3
  5V: J1.5V, S2.Pin_1, S2.Pin_2, S3.Pin_1, S3.Pin_2, S4.Pin_1, S4.Pin_2, S5.Pin_1, S5.Pin_2, S6.Pin_1, S6.Pin_2, S7.Pin_1, S7.Pin_2, S8.Pin_1, S8.Pin_2, S9.Pin_1, S9.Pin_2, IC1.pin11, IC1.pin19, IC1.pin21, LED2.anode, LED3.anode, LED4.anode, LED5.anode, LED6.anode, LED7.anode, LED8.anode, LED9.anode, Part1.C8, Part1.C9, Part1.C10, Part1.C11, Part1.C12, Part1.C13, Part1.C14, Part1.C15, Part1.VCC, C1.+, C2.1, RE1.InputCommon2, IC3.pin9, IC3.pin11, IC3.pin14, C7.1
  N12: J1.GND#1188, IC1.pin22, IC1.pin27, Part1.GND, R1.Pin_1, R2.Pin_1, R3.Pin_1, R4.Pin_1, R5.Pin_1, R6.Pin_1, R7.Pin_1, R8.Pin_1, R9.Pin_1, SP1.+, IC3.pin7, R10.Pin_1, SP2.+, SP3.+, SP4.+, R12.Pin_1, R14.Pin_1, R16.Pin_1, C6.0
  N13: S2.Pin_3, S2.Pin_4, R1.Pin_0
  N14: S3.Pin_3, S3.Pin_4, R8.Pin_0
  N15: S4.Pin_3, S4.Pin_4, R7.Pin_0
  N16: S5.Pin_3, S5.Pin_4, R4.Pin_0
  N17: S6.Pin_3, S6.Pin_4, R2.Pin_0
  N18: S7.Pin_3, S7.Pin_4, R3.Pin_0
  N19: S8.Pin_3, S8.Pin_4, R5.Pin_0
  N20: S9.Pin_3, S9.Pin_4, R6.Pin_0
  N21: IC1.pin7, LED2.cathode
  N22: IC1.pin8, LED3.cathode
  N23: IC1.pin9, LED4.cathode
  N24: IC1.pin10, LED5.cathode
  N25: IC1.pin12, LED7.cathode
  N26: IC1.pin13, LED8.cathode
  N27: IC1.pin14, LED9.cathode
  N28: IC1.pin18, JP1.5
  N29: IC1.pin20, R9.Pin_0
  N30: IC1.pin23, JP1.4
  N31: IC1.pin24, JP1.3
  N32: IC1.pin25, JP1.2
  N33: IC1.pin26, JP1.1
  N34: SP1.-, R12.Pin_0, R13.Pin_1
  N35: IC3.pin1, C4.1, R18.Pin_0
  N36: IC3.pin2, R15.Pin_0, R18.Pin_1
  N37: IC3.pin3, C3.1, R19.Pin_0
  N38: IC3.pin4, R17.Pin_0, R19.Pin_1
  N39: IC3.pin5, C5.1, R20.Pin_0
  N40: IC3.pin6, R13.Pin_0, R20.Pin_1
  N41: IC3.pin12, R11.Pin_0, R21.Pin_0
  N42: IC3.pin13, C6.1, R21.Pin_1
  N43: R10.Pin_0, R11.Pin_1, SP4.-
  N44: SP2.-, R14.Pin_0, R15.Pin_1
  N45: SP3.-, R16.Pin_0, R17.Pin_1
  N46: C3.0, JP2.4
  N47: C4.0, JP2.5
  N48: C5.0, JP2.3
  N49: C7.0, JP2.6

notes:
  OpenBeats Breadboard Diagram V1.0
  On/Off Beat Buttons & Respective LEDs
  B1-USER is used as stop/start button in prototype
  SUBJECT TO CHANGE / FOR REVIEW:
  - Pull-Down Resistors in beat buttons
  - 47kOhm voltage divider for oscilator
  - Lower channel LED driver
  - Lower channel button multiplexer
  R = 39.06 / Imax
  (With Imax per 1 LED) (Resistor going into LED driver)
  TO BE CONNECTED
  INSTURMENT SELECTOR
  (for each possible hex combo, common terminals are connected to pins 1-4 corresponding to first 4 bits of hex code. Total of 16 possible combinations)
  Oscilator V1 (Simple CMOS Inverter)
  - Capacitor and Resistor specs on inverter subject to change based on sound requirements
  1/5 input V Peak-To-Peak
  Avaliable digital pins:
  - 9 on MCU
  Needed digital pins:
  - 8 on MCU
  (For unconnected pins)
